// Logisim project CRC.circ as structural Verilog: 2 circuits, main circuit CRC
module CRC (
  input  [7:0] in_1,
  input  [3:0] in_2,
  output [10:0] out_3
);

  wire [2:0] n4digits_mod2_1_out_3, n4digits_mod2_2_out_3, n4digits_mod2_3_out_3, n4digits_mod2_4_out_3,
       n4digits_mod2_5_out_3, n4digits_mod2_7_out_3;
  wire [3:1] n4digits_mod2_6_out_3;

  _4digits_mod2 u_4digits_mod2_1 (.in_1(in_1[7:4]), .in_2(in_2), .out_3(n4digits_mod2_1_out_3));
  _4digits_mod2 u_4digits_mod2_2 (.in_1({n4digits_mod2_1_out_3, in_1[3]}), .in_2(in_2), .out_3(n4digits_mod2_2_out_3));
  _4digits_mod2 u_4digits_mod2_3 (.in_1({n4digits_mod2_2_out_3, in_1[2]}), .in_2(in_2), .out_3(n4digits_mod2_3_out_3));
  _4digits_mod2 u_4digits_mod2_4 (.in_1({n4digits_mod2_3_out_3, in_1[1]}), .in_2(in_2), .out_3(n4digits_mod2_4_out_3));
  _4digits_mod2 u_4digits_mod2_5 (.in_1({n4digits_mod2_4_out_3, in_1[0]}), .in_2(in_2), .out_3(n4digits_mod2_5_out_3));
  _4digits_mod2 u_4digits_mod2_6 (.in_1({n4digits_mod2_5_out_3, 1'b0}), .in_2(in_2), .out_3(n4digits_mod2_6_out_3));
  _4digits_mod2 u_4digits_mod2_7 (.in_1({n4digits_mod2_6_out_3, 1'b0}), .in_2(in_2), .out_3(n4digits_mod2_7_out_3));
  _4digits_mod2 u_4digits_mod2_8 (.in_1({n4digits_mod2_7_out_3, 1'b0}), .in_2(in_2), .out_3(out_3[2:0]));

  assign out_3[10:3] = in_1;

  // Other names for the same wires on the sheet: A3 = in_1[3]; src[7:0] = in_1; A2 = in_1[2]; A1 = in_1[1];
  //   A0 = in_1[0]; div[3:0] = in_2; halfans[2:0] = out_3[2:0]; A4 = in_1[4]; A5 = in_1[5]; A6 = in_1[6];
  //   A7 = in_1[7]
endmodule

module _4digits_mod2 (
  input  [3:0] in_1,
  input  [3:0] in_2,
  output [2:0] out_3
);

  wire bitselector_1_out;
  wire [3:0] xor_1_out;
  wire [3:3] multiplexer_1_out;

  BitSelector #(.width(4)) bitselector_1 (.in(in_1), .out(bitselector_1_out), .sel(2'b11));
  assign xor_1_out = in_1 ^ in_2;  // XOR_Gate xor_1, 4 bits wide
  Multiplexer #(.width(4)) multiplexer_1 (
    .in0(in_1), .in1(xor_1_out), .out({multiplexer_1_out[3], out_3}), .sel(bitselector_1_out));  // open: en
endmodule
