// Logisim project FSM.circ as structural Verilog: 4 circuits, main circuit fsm
module fsm (
  input  CLR,
  input  [1:0] In,
  output out_3
);

  wire clk, comparator_1_eq, eqac_1_out_2;
  wire [1:0] multiplexer_1_out, register_1_q, stattrans_1_out_3;

  Clock clock_1 (.out(clk));
  statTrans stattrans_1 (.in_1(In), .in_2(register_1_q), .out_3(stattrans_1_out_3));
  Register #(.width(2)) register_1 (.D(multiplexer_1_out), .en(1'b1), .Q(register_1_q), .clk(clk));  // open: clr
  Multiplexer #(.width(2)) multiplexer_1 (
    .in0(stattrans_1_out_3), .in1(2'b00), .out(multiplexer_1_out), .sel(CLR));  // open: en
  eqac eqac_1 (.in_1(In), .out_2(eqac_1_out_2));
  Comparator #(.width(2)) comparator_1 (.a(register_1_q), .b(2'b10), .eq(comparator_1_eq));  // open: gt, lt
  and and_1 (out_3, eqac_1_out_2, comparator_1_eq);

  // Other names for the same wires on the sheet: reset = CLR
endmodule

module eqac (
  input  [1:0] in_1,
  output out_2
);

  wire comparator_1_eq, comparator_2_eq;

  Comparator #(.width(2), .mode("unsigned")) comparator_1 (.a(in_1), .b(2'b10), .eq(comparator_1_eq));  // open: gt, lt
  Comparator #(.width(2), .mode("unsigned")) comparator_2 (.a(in_1), .b(2'b00), .eq(comparator_2_eq));  // open: gt, lt
  or or_1 (out_2, comparator_1_eq, comparator_2_eq);
endmodule

module tes (
  input  in_1,
  input  in_2,
  input  in_3,
  input  in_4,
  output out_5,
  output out_6,
  output out_7
);

  // AND_Gate and_1 has open pins: in0=in_2, in4=in_4, out=open
endmodule

module statTrans (
  input  [1:0] in_1,
  input  [1:0] in_2,
  output [1:0] out_3
);

  wire comparator_1_eq, comparator_2_eq, comparator_3_eq, comparator_4_eq, eqac_1_out_2, eqac_2_out_2;
  wire [1:0] multiplexer_1_out, multiplexer_2_out, multiplexer_3_out, multiplexer_4_out, multiplexer_5_out,
       multiplexer_6_out;

  Multiplexer #(.width(2), .disabled(0)) multiplexer_1 (
    .in0(2'b00), .in1(2'b10), .out(multiplexer_1_out), .sel(eqac_1_out_2));  // open: en
  eqac eqac_1 (.in_1(in_1), .out_2(eqac_1_out_2));
  Multiplexer #(.width(2), .disabled(0)) multiplexer_2 (
    .in0(2'b00), .in1(2'b01), .out(multiplexer_2_out), .sel(comparator_1_eq));  // open: en
  Comparator #(.width(2), .mode("unsigned")) comparator_1 (.a(in_1), .b(2'b01), .eq(comparator_1_eq));  // open: gt, lt
  eqac eqac_2 (.in_1(in_1), .out_2(eqac_2_out_2));
  Comparator #(.width(2), .mode("unsigned")) comparator_2 (.a(in_1), .b(2'b01), .eq(comparator_2_eq));  // open: gt, lt
  Multiplexer #(.width(2), .disabled(0)) multiplexer_3 (
    .in0(2'b00), .in1(2'b01), .out(multiplexer_3_out), .sel(comparator_3_eq));  // open: en
  Comparator #(.width(2), .mode("unsigned")) comparator_3 (.a(in_1), .b(2'b01), .eq(comparator_3_eq));  // open: gt, lt
  Multiplexer #(.width(2), .disabled(0)) multiplexer_4 (
    .in0(multiplexer_1_out), .in1(2'b01), .out(multiplexer_4_out), .sel(comparator_4_eq));  // open: en
  Comparator #(.width(2), .mode("unsigned")) comparator_4 (.a(in_1), .b(2'b01), .eq(comparator_4_eq));  // open: gt, lt
  Multiplexer #(.width(2), .disabled(0)) multiplexer_5 (
    .in0(multiplexer_2_out), .in1(2'b00), .out(multiplexer_5_out), .sel(eqac_2_out_2));  // open: en
  Multiplexer #(.width(2), .disabled(0)) multiplexer_6 (
    .in0(2'b00), .in1(2'b01), .out(multiplexer_6_out), .sel(comparator_2_eq));  // open: en
  Multiplexer #(.select(2), .width(2)) multiplexer_7 (
    .in0(multiplexer_3_out), .in1(multiplexer_4_out), .in2(multiplexer_5_out), .in3(multiplexer_6_out),
    .out(out_3), .sel(in_2));  // open: en

  // Other names for the same wires on the sheet: inp[1:0] = in_1; reg[1:0] = in_2
endmodule
