// Logisim project Navigation.circ as structural Verilog: 3 circuits, main circuit navigation
module navigation (
  input  [1:0] dir,
  input  clk,
  input  reset,
  output arrive,
  output hit
);

  wire clock_1_out, fsm_1_hit;
  wire [2:0] fsm_1_next_stat, register_2_q;

  Clock clock_1 (.out(clock_1_out));
  FSM fsm_1 (.in_1(dir), .in_2(register_2_q), .hit(fsm_1_hit), .next_stat(fsm_1_next_stat));
  Register #(.width(1)) register_1 (.D(fsm_1_hit), .Q(hit), .clk(clk), .clr(reset));  // open: en
  Register #(.width(3)) register_2 (.D(fsm_1_next_stat), .Q(register_2_q), .clk(clk), .clr(reset));  // open: en
  Comparator #(.width(3)) comparator_1 (.a(3'b100), .b(register_2_q), .eq(arrive));  // open: gt, lt
endmodule

module FSM (
  input  [1:0] in_1,
  input  [2:0] in_2,
  output hit,
  output [2:0] next_stat
);

  wire multiplexer_5_out, multiplexer_6_out, multiplexer_7_out, multiplexer_8_out, multiplexer_9_out;
  wire [2:0] multiplexer_1_out, multiplexer_2_out, multiplexer_3_out, multiplexer_4_out;

  Multiplexer #(.select(2), .width(3)) multiplexer_1 (
    .in0(3'b001), .in1(3'b000), .in2(3'b000), .in3(3'b000), .out(multiplexer_1_out), .sel(in_1));  // open: en
  Multiplexer #(.select(2), .width(3)) multiplexer_2 (
    .in0(3'b011), .in1(3'b010), .in2(3'b000), .in3(3'b001), .out(multiplexer_2_out), .sel(in_1));  // open: en
  Multiplexer #(.select(2), .width(3)) multiplexer_3 (
    .in0(3'b100), .in1(3'b010), .in2(3'b010), .in3(3'b001), .out(multiplexer_3_out), .sel(in_1));  // open: en
  Multiplexer #(.select(2), .width(3)) multiplexer_4 (
    .in0(3'b011), .in1(3'b100), .in2(3'b001), .in3(3'b011), .out(multiplexer_4_out), .sel(in_1));  // open: en
  Multiplexer #(.select(2)) multiplexer_5 (
    .in0(1'b1), .in1(1'b0), .in2(1'b0), .in3(1'b0), .out(multiplexer_5_out), .sel(in_1));  // open: en
  Multiplexer #(.select(2)) multiplexer_6 (
    .in0(1'b1), .in1(1'b1), .in2(1'b1), .in3(1'b0), .out(multiplexer_6_out), .sel(in_1));  // open: en
  Multiplexer #(.select(2)) multiplexer_7 (
    .in0(1'b1), .in1(1'b0), .in2(1'b0), .in3(1'b1), .out(multiplexer_7_out), .sel(in_1));  // open: en
  Multiplexer #(.select(2)) multiplexer_8 (
    .in0(1'b0), .in1(1'b1), .in2(1'b1), .in3(1'b0), .out(multiplexer_8_out), .sel(in_1));  // open: en
  Multiplexer #(.select(3)) multiplexer_9 (
    .in0(multiplexer_5_out), .in1(multiplexer_6_out), .in2(multiplexer_7_out), .in3(multiplexer_8_out),
    .in4(1'b1), .out(multiplexer_9_out), .sel(in_2));  // open: in5, in6, in7, en
  Multiplexer #(.select(3), .width(3)) multiplexer_10 (
    .in0(multiplexer_1_out), .in1(multiplexer_2_out), .in2(multiplexer_3_out), .in3(multiplexer_4_out),
    .in4(3'b000), .in5(3'b000), .in6(3'b000), .in7(3'b000), .out(next_stat), .sel(in_2));  // open: en
  not not_1 (hit, multiplexer_9_out);

  // Other names for the same wires on the sheet: dir[1:0] = in_1; stat[2:0] = in_2
endmodule

module test (
  output [1:0] dir,
  output rst,
  output arv,
  output hi,
  output out_5
);

  wire clock_1_out;
  wire [15:0] counter_1_q;

  Clock clock_1 (.out(clock_1_out));
  Counter #(.width(16), .max('hffff)) counter_1 (
    .Q(counter_1_q), .carry(out_5), .clk(clock_1_out));  // open: load, D, count, clr
  ROM #(.addrWidth(16), .dataWidth(2)) rom_1 (.addr(counter_1_q), .data(dir));  // open: sel
  Counter #(.width(1), .max('h1), .ongoal("stay")) counter_2 (
    .carry(rst), .clk(clock_1_out));  // open: load, D, count, Q, clr
  navigation navigation_1 (.dir(dir), .clk(clock_1_out), .reset(1'b0), .arrive(arv), .hit(hi));

  // Notes on the sheet:
  //   contents of rom_1 (hex, n*v repeats v):
  //   0 1 0 3 0 0 1 0 0 3 1 0 0 0 2 2 1 3 2 3 2 2 0 2 1 0 3 3 2 0 0 3
endmodule
