// Logisim project ftoi.circ as structural Verilog: 1 circuit, main circuit ftoi
module ftoi (
  input  [15:0] float,
  output [31:0] \int 
);

  wire comparator_1_lt, denorm, or_1_out, or_2_out, zero;
  wire [4:0] E, negator_1_out;
  wire [31:0] multiplexer_1_out, multiplexer_2_out, negator_2_out, shifter_1_out, shifter_2_out,
       shifter_3_out;

  // Probe on {22'h1, float[9:0]}
  Negator #(.width(5)) negator_1 (.in(E), .out(negator_1_out));
  Comparator #(.width(5)) comparator_1 (.a(E), .b({5{1'b0}}), .lt(comparator_1_lt));  // open: gt, eq
  and isinf_nan (zero, float[10], float[11], float[12], float[13], float[14]);
  or or_1 (or_1_out, float[10], float[11], float[12], float[13], float[14]);
  not not_1 (denorm, or_1_out);
  Subtractor #(.width(5)) subtractor_1 (.a(float[14:10]), .b(5'b01111), .out(E));  // open: bin, bout
  Shifter #(.width(32)) shifter_1 (.in({22'h1, float[9:0]}), .\dist (E), .out(shifter_1_out));
  Shifter #(.width(32), .shift("lr")) shifter_2 (.in({22'h1, float[9:0]}), .\dist (negator_1_out), .out(shifter_2_out));
  Multiplexer #(.width(32)) multiplexer_1 (
    .in0(shifter_1_out), .in1(shifter_2_out), .out(multiplexer_1_out), .sel(comparator_1_lt));  // open: en
  Shifter #(.width(32), .shift("lr")) shifter_3 (.in(multiplexer_1_out), .\dist (5'b01010), .out(shifter_3_out));
  Negator #(.width(32)) negator_2 (.in(shifter_3_out), .out(negator_2_out));
  Multiplexer #(.width(32)) multiplexer_2 (
    .in0(shifter_3_out), .in1(negator_2_out), .out(multiplexer_2_out), .sel(float[15]));  // open: en
  or or_2 (or_2_out, zero, denorm);
  Multiplexer #(.width(32)) multiplexer_3 (
    .in0(multiplexer_2_out), .in1({32{1'b0}}), .out(\int ), .sel(or_2_out));  // open: en

  // Other names for the same wires on the sheet: frac[9:0] = float[9:0]; sign = float[15]
endmodule
