// Logisim project 4-正则表达式匹配.circ as structural Verilog: 3 circuits, main circuit fsm
module fsm (
  input  CLR,
  input  [1:0] In,
  input  in_3,
  output z
);

  wire and_1_out, clock_1_out, clock_2_out, multiplexer_1_out;
  wire [1:0] multiplexer_2_out, state, state_transfer_1_ns0;

  Multiplexer #(.enable("false")) multiplexer_1 (.in0(in_3), .in1(1'b0), .out(multiplexer_1_out), .sel(CLR));
  Register #(.width(1)) register_1 (.D(multiplexer_1_out), .clk(clock_1_out));  // open: en, Q, clr
  Clock clock_1 (.out(clock_1_out));
  state_transfer state_transfer_1 (
    .s1(state[1]), .Ns1(state_transfer_1_ns0[1]), .s0(state[0]), .In1(In[1]), .Ns0(state_transfer_1_ns0[0]),
    .In0(In[0]));
  Multiplexer #(.width(2), .enable("false")) multiplexer_2 (
    .in0(state_transfer_1_ns0), .in1(2'b00), .out(multiplexer_2_out), .sel(CLR));
  Clock clock_2 (.out(clock_2_out));
  Register #(.width(1)) register_2 (.D(in_3), .clk(clock_1_out), .clr(and_1_out));  // open: en, Q
  and and_1 (and_1_out, clock_1_out, CLR);
  Register #(.width(2)) register_3 (.D(multiplexer_2_out), .Q(state), .clk(clock_2_out));  // open: en, clr
  output_logic output_logic_1 (.s1(state[1]), .s0(state[0]), .In1(In[1]), .In0(In[0]), .z(z));

  // Other names for the same wires on the sheet: status = in_3

  // Notes on the sheet:
  //   正确的同步复位
  //   复位部分展示
  //   状态转移部分
  //   错误的同步复位
  //   输出逻辑
endmodule

module state_transfer (
  input  s1,
  input  s0,
  input  In1,
  input  In0,
  output Ns1,
  output Ns0
);

  wire and_2_out, and_3_out, not_1_out, not_2_out, not_3_out, not_4_out, not_5_out, not_6_out;

  not not_1 (not_1_out, s1);
  and and_1 (Ns1, not_1_out, s0, not_2_out);
  not not_2 (not_2_out, In0);
  not not_3 (not_3_out, s1);
  and and_2 (and_2_out, not_3_out, not_4_out, In0);
  not not_4 (not_4_out, In1);
  not not_5 (not_5_out, s0);
  not not_6 (not_6_out, In1);
  and and_3 (and_3_out, not_5_out, not_6_out, In0);
  or or_1 (Ns0, and_2_out, and_3_out);
endmodule

module output_logic (
  input  s1,
  input  s0,
  input  In1,
  input  In0,
  output z
);

  wire not_1_out, not_2_out;

  not not_1 (not_1_out, s0);
  not not_2 (not_2_out, In0);
  and and_1 (z, s1, not_1_out, not_2_out);
endmodule
