// Logisim project P3L.circ as structural Verilog: 8 circuits, main circuit GRF
module GRF (
  input  clk,
  input  reset,
  input  WE,
  input  [4:0] A1,
  input  [4:0] A2,
  input  [4:0] A3,
  input  [31:0] WD,
  output [31:0] RD1,
  output [31:0] RD2
);

  wire [31:0] i1, i2, i3, i4, i5, i6, i7, i8, i9, i10, i11, i12, i13, i14, i15, i16, i17, i18, i19, i20, i21,
       i22, i23, i24, i25, i26, i27, i28, i29, i30, i31, o0, o1, o2, o3, o4, o5, o6, o7, o8, o9, o10, o11,
       o12, o13, o14, o15, o16, o17, o18, o19, o20, o21, o22, o23, o24, o25, o26, o27, o28, o29, o30, o31;

  Clock clock_1 ();  // open: out
  Register #(.width(32)) register_1 (.D({32{1'b0}}), .en(WE), .Q(o0), .clk(clk), .clr(reset));
  Register #(.width(32)) register_2 (.D(i5), .en(WE), .Q(o5), .clk(clk), .clr(reset));
  Register #(.width(32)) register_3 (.D(i10), .en(WE), .Q(o10), .clk(clk), .clr(reset));
  Register #(.width(32)) register_4 (.D(i15), .en(WE), .Q(o15), .clk(clk), .clr(reset));
  Register #(.width(32)) register_5 (.D(i20), .en(WE), .Q(o20), .clk(clk), .clr(reset));
  Register #(.width(32)) register_6 (.D(i25), .en(WE), .Q(o25), .clk(clk), .clr(reset));
  Register #(.width(32)) register_7 (.D(i30), .en(WE), .Q(o30), .clk(clk), .clr(reset));
  Multiplexer #(.select(5), .width(32)) multiplexer_1 (
    .in0(o0), .in1(o1), .in2(o2), .in3(o3), .in4(o4), .in5(o5), .in6(o6), .in7(o7), .in8(o8), .in9(o9),
    .in10(o10), .in11(o11), .in12(o12), .in13(o13), .in14(o14), .in15(o15), .in16(o16), .in17(o17),
    .in18(o18), .in19(o19), .in20(o20), .in21(o21), .in22(o22), .in23(o23), .in24(o24), .in25(o25),
    .in26(o26), .in27(o27), .in28(o28), .in29(o29), .in30(o30), .in31(o31), .out(RD1), .sel(A1));  // open: en
  Demultiplexer #(.select(5), .width(32), .tristate("true")) demultiplexer_1 (
    .out1(i1), .out2(i2), .out3(i3), .out4(i4), .out5(i5), .out6(i6), .out7(i7), .out8(i8), .out9(i9),
    .out10(i10), .out11(i11), .out12(i12), .out13(i13), .out14(i14), .out15(i15), .out16(i16), .out17(i17),
    .out18(i18), .out19(i19), .out20(i20), .out21(i21), .out22(i22), .out23(i23), .out24(i24), .out25(i25),
    .out26(i26), .out27(i27), .out28(i28), .out29(i29), .out30(i30), .out31(i31), .in(WD), .sel(A3));  // open: out0, en
  Register #(.width(32)) register_8 (.D(i1), .en(WE), .Q(o1), .clk(clk), .clr(reset));
  Register #(.width(32)) register_9 (.D(i6), .en(WE), .Q(o6), .clk(clk), .clr(reset));
  Register #(.width(32)) register_10 (.D(i11), .en(WE), .Q(o11), .clk(clk), .clr(reset));
  Register #(.width(32)) register_11 (.D(i16), .en(WE), .Q(o16), .clk(clk), .clr(reset));
  Register #(.width(32)) register_12 (.D(i21), .en(WE), .Q(o21), .clk(clk), .clr(reset));
  Register #(.width(32)) register_13 (.D(i26), .en(WE), .Q(o26), .clk(clk), .clr(reset));
  Register #(.width(32)) register_14 (.D(i31), .en(WE), .Q(o31), .clk(clk), .clr(reset));
  Register #(.width(32)) register_15 (.D(i2), .en(WE), .Q(o2), .clk(clk), .clr(reset));
  Register #(.width(32)) register_16 (.D(i7), .en(WE), .Q(o7), .clk(clk), .clr(reset));
  Register #(.width(32)) register_17 (.D(i12), .en(WE), .Q(o12), .clk(clk), .clr(reset));
  Register #(.width(32)) register_18 (.D(i17), .en(WE), .Q(o17), .clk(clk), .clr(reset));
  Register #(.width(32)) register_19 (.D(i22), .en(WE), .Q(o22), .clk(clk), .clr(reset));
  Register #(.width(32)) register_20 (.D(i27), .en(WE), .Q(o27), .clk(clk), .clr(reset));
  Register #(.width(32)) register_21 (.D(i3), .en(WE), .Q(o3), .clk(clk), .clr(reset));
  Register #(.width(32)) register_22 (.D(i8), .en(WE), .Q(o8), .clk(clk), .clr(reset));
  Register #(.width(32)) register_23 (.D(i13), .en(WE), .Q(o13), .clk(clk), .clr(reset));
  Register #(.width(32)) register_24 (.D(i18), .en(WE), .Q(o18), .clk(clk), .clr(reset));
  Register #(.width(32)) register_25 (.D(i23), .en(WE), .Q(o23), .clk(clk), .clr(reset));
  Register #(.width(32)) register_26 (.D(i28), .en(WE), .Q(o28), .clk(clk), .clr(reset));
  Multiplexer #(.select(5), .width(32)) multiplexer_2 (
    .in0(o0), .in1(o1), .in2(o2), .in3(o3), .in4(o4), .in5(o5), .in6(o6), .in7(o7), .in8(o8), .in9(o9),
    .in10(o10), .in11(o11), .in12(o12), .in13(o13), .in14(o14), .in15(o15), .in16(o16), .in17(o17),
    .in18(o18), .in19(o19), .in20(o20), .in21(o21), .in22(o22), .in23(o23), .in24(o24), .in25(o25),
    .in26(o26), .in27(o27), .in28(o28), .in29(o29), .in30(o30), .in31(o31), .out(RD2), .sel(A2));  // open: en
  Register #(.width(32)) register_27 (.D(i4), .en(WE), .Q(o4), .clk(clk), .clr(reset));
  Register #(.width(32)) register_28 (.D(i9), .en(WE), .Q(o9), .clk(clk), .clr(reset));
  Register #(.width(32)) register_29 (.D(i14), .en(WE), .Q(o14), .clk(clk), .clr(reset));
  Register #(.width(32)) register_30 (.D(i19), .en(WE), .Q(o19), .clk(clk), .clr(reset));
  Register #(.width(32)) register_31 (.D(i24), .en(WE), .Q(o24), .clk(clk), .clr(reset));
  Register #(.width(32)) register_32 (.D(i29), .en(WE), .Q(o29), .clk(clk), .clr(reset));
endmodule

module main (
  input  in_1,
  output [31:0] out_2,
  output out_3,
  output [4:0] out_4,
  output [31:0] out_5,
  output out_6,
  output [4:0] out_7,
  output [31:0] out_8
);

  wire ALUSrc, clk, cmp, nPC_sel, RegDst;
  wire [1:0] ExtOp, RAMWidth, toReg;
  wire [2:0] ALUctr;
  wire [4:0] rd, rs, rt, shamt;
  wire [5:0] func, optCode;
  wire [15:0] spl_1_imm16;
  wire [31:0] ALURes, imm32, MemRD, multiplexer_3_out, PC_4, RegRD1;

  Clock clock_1 (.out(clk));
  IFU ifu_1 (
    .clk(clk), .reset(in_1), .imm32(imm32), .PC_jr(RegRD1), .out_8(PC_4), .out_9(out_2), .nPC_sel(nPC_sel),
    .in_5(cmp));  // open: in_4
  // Probe on PC_4
  Multiplexer #(.width(5)) multiplexer_1 (.in0(rt), .in1(rd), .out(out_4), .sel(RegDst));  // open: en
  Multiplexer #(.select(2), .width(32)) multiplexer_2 (
    .in0({ALURes[31:7], out_7, ALURes[1:0]}), .in1(MemRD), .in2(imm32), .in3(PC_4), .out(out_5), .sel(toReg));  // open: en
  // Probe on out_2
  SPL spl_1 (
    .Option(out_2), .func(func), .shamt(shamt), .rd(rd), .rt(rt), .rs(rs), .optCode(optCode),
    .imm16(spl_1_imm16));
  GRF grf_1 (.clk(clk), .reset(in_1), .WE(out_3), .A1(rs), .A2(rt), .A3(out_4), .WD(out_5), .RD1(RegRD1), .RD2(out_8));
  DM dm_1 (
    .clk(clk), .reset(in_1), .WE(out_6), .A({ALURes[31:7], out_7, ALURes[1:0]}), .WD(out_8), .RD(MemRD),
    .\bit (RAMWidth));
  // Probe on imm32
  EXT ext_1 (.imm16(spl_1_imm16), .sign(ExtOp), .out_3(imm32));
  Controller controller_1 (
    .optCode(optCode), .\function (func), .out_3(RegDst), .out_4(ALUSrc), .out_5(toReg), .out_6(out_3),
    .out_7(out_6), .out_8(nPC_sel), .out_9(ExtOp), .out_10(ALUctr), .out_11(RAMWidth));  // open: out_12
  Multiplexer #(.width(32)) multiplexer_3 (
    .in0(out_8), .in1(imm32), .out(multiplexer_3_out), .sel(ALUSrc));  // open: en
  ALU alu_1 (.A1(RegRD1), .A2(multiplexer_3_out), .op(ALUctr), .res({ALURes[31:7], out_7, ALURes[1:0]}), .out_5(cmp));
  // Probe on out_2

  // Other names for the same wires on the sheet: ALURes[6:2] = out_7; instr[31:0] = out_2; MemWrite = out_6;
  //   RegAddr[4:0] = out_4; RegData[31:0] = out_5; RegRD2[31:0] = out_8; RegWrite = out_3; reset = in_1
endmodule

module IFU (
  input  clk,
  input  reset,
  input  nPC_sel,
  input  in_4,
  input  in_5,
  input  [31:0] imm32,
  input  [31:0] PC_jr,
  output [31:0] out_8,
  output [31:0] out_9
);

  wire [31:0] imm32_t, multiplexer_1_out, NPC, PC, shifter_1_out;

  Shifter #(.width(32)) shifter_1 (.in(imm32), .\dist (5'b00010), .out(shifter_1_out));
  Subtractor #(.width(32)) subtractor_1 (.b(32'h3000));  // open: a, out, bin, bout
  Adder #(.width(32)) adder_1 (.b(32'h3000));  // open: a, out, cin, cout
  Adder #(.width(32)) adder_2 (.a(shifter_1_out), .b(out_8), .out(imm32_t));  // open: cin, cout
  Multiplexer #(.width(32)) multiplexer_1 (
    .in0(out_8), .in1(imm32_t), .out(multiplexer_1_out), .sel(in_5));  // open: en
  Adder #(.width(32)) adder_3 (.a(PC), .b(32'h4), .out(out_8));  // open: cin, cout
  Register #(.width(32)) u_PC (.D(NPC), .Q(PC), .clk(clk), .clr(reset));  // open: en
  Multiplexer #(.width(32)) multiplexer_2 (.in0(out_8), .in1(multiplexer_1_out), .out(NPC), .sel(nPC_sel));  // open: en
  ROM #(.addrWidth(5), .dataWidth(32)) rom_1 (.addr(PC[6:2]), .data(out_9));  // open: sel

  // Other names for the same wires on the sheet: cmp = in_5; ins[31:0] = out_9; not = in_4; PC_4[31:0] = out_8

  // Notes on the sheet:
  //   contents of rom_1 (hex, n*v repeats v):
  //   341c0000 341d0000 34013456 210820 8c010004 ac010004 3c027878 411822 3c051234 34040005 0 ac85ffff
  //   8c83ffff 10650001 1000000d 34670404 10e3000b 0 3c087777 3508ffff 80022 34001100 e65020 34080000
  //   34090001 340a0001 10a4020 1109fffe 1000ffff
endmodule

module EXT (
  input  [15:0] imm16,
  input  [1:0] sign,
  output [31:0] out_3
);

  wire [31:0] bit_extender_1_out, bit_extender_2_out, shifter_1_out;

  assign bit_extender_1_out = {{16{1'b0}}, imm16};  // Bit_Extender bit_extender_1
  assign bit_extender_2_out = {{16{imm16[15]}}, imm16};  // Bit_Extender bit_extender_2
  Shifter #(.width(32)) shifter_1 (.in(bit_extender_1_out), .\dist (5'b10000), .out(shifter_1_out));
  Multiplexer #(.select(2), .width(32)) multiplexer_1 (
    .in0(bit_extender_1_out), .in1(bit_extender_2_out), .in2(shifter_1_out), .out(out_3), .sel(sign));  // open: in3, en
endmodule

module ALU (
  input  [31:0] A1,
  input  [31:0] A2,
  input  [2:0] op,
  output [31:0] res,
  output out_5
);

  wire eq, gt, lt, or_1_out;
  wire [4:0] bit_extender_1_out;
  wire [31:0] add, \and , \or , sll, sub;

  Bit_Extender #(.in_width(32), .out_width(5)) bit_extender_1 (.in(A1), .out(bit_extender_1_out));
  // Probe on bit_extender_1_out
  or or_1 (or_1_out, eq, gt);
  Adder #(.width(32)) adder_1 (.a(A1), .b(A2), .out(add));  // open: cin, cout
  Subtractor #(.width(32)) subtractor_1 (.a(A1), .b(A2), .out(sub));  // open: bin, bout
  assign \and  = A1 & A2;  // AND_Gate and_1, 32 bits wide
  assign \or  = A1 | A2;  // OR_Gate or_2, 32 bits wide
  Shifter #(.width(32)) shifter_1 (.in(A2), .\dist (bit_extender_1_out), .out(sll));
  Multiplexer #(.select(3), .width(32)) multiplexer_1 (
    .in0(add), .in1(sub), .in2(\and ), .in3(\or ), .in4(sll), .out(res), .sel(op));  // open: in5, in6, in7, en
  Multiplexer #(.select(3)) multiplexer_2 (
    .in0(eq), .in1(gt), .in2(lt), .in3(or_1_out), .out(out_5), .sel(op));  // open: in4, in5, in6, in7, en
  Comparator #(.width(32)) comparator_1 (.a(A1), .b(A2), .gt(gt), .eq(eq), .lt(lt));

  // Notes on the sheet:
  //   000+
  //   001-
  //   010&
  //   011|
  //   A2<<A1
  //   100<<
  //   000 eq
  //   001gt
  //   010lt
endmodule

module DM (
  input  clk,
  input  [1:0] \bit ,
  input  reset,
  input  WE,
  input  [31:0] A,
  input  [31:0] WD,
  output [31:0] RD
);

  wire [7:0] multiplexer_1_out, R0, R1, R2, R3;
  wire [31:0] multiplexer_2_out, multiplexer_3_out, multiplexer_4_out, ND;

  // Probe on A[6:2]
  RAM #(.addrWidth(5), .dataWidth(32), .bus("separate")) ram_1 (
    .addr(A[6:2]), .din(ND), .data({R3, R2, R1, R0}), .str(WE), .clk(clk), .clr(reset));  // open: sel, ld
  Multiplexer #(.select(2), .width(8)) multiplexer_1 (
    .in0(R0), .in1(R1), .in2(R2), .in3(R3), .out(multiplexer_1_out), .sel(A[1:0]));  // open: en
  Multiplexer #(.select(2), .width(32)) multiplexer_2 (
    .in0({{16{1'b0}}, R1, R0}), .in2({{16{1'b0}}, R3, R2}), .out(multiplexer_2_out), .sel(A[1:0]));  // open: in1, in3, en
  Multiplexer #(.select(2), .width(32)) multiplexer_3 (
    .in0({R3, R2, WD[15:0]}), .in2({WD[15:0], R1, R0}), .out(multiplexer_3_out), .sel(A[1:0]));  // open: in1, in3, en
  Multiplexer #(.select(2), .width(32)) multiplexer_4 (
    .in0({R3, R2, R1, WD[7:0]}), .in1({R3, R2, WD[7:0], R0}), .in2({R3, WD[7:0], R1, R0}),
    .in3({WD[7:0], R2, R1, R0}), .out(multiplexer_4_out), .sel(A[1:0]));  // open: en
  Multiplexer #(.select(2), .width(32)) multiplexer_5 (
    .in0(WD), .in1(multiplexer_3_out), .in2(multiplexer_4_out), .out(ND), .sel(\bit ));  // open: in3, en
  Multiplexer #(.select(2), .width(32)) multiplexer_6 (
    .in0({R3, R2, R1, R0}), .in1(multiplexer_2_out), .in2({{24{1'b0}}, multiplexer_1_out}), .out(RD),
    .sel(\bit ));  // open: in3, en

  // Other names for the same wires on the sheet: RD_t[31:0] = {R3, R2, R1, R0}; W0[7:0] = WD[7:0]; W1[7:0] = WD[15:8];
  //   A2[1:0] = A[1:0]; O[31:0] = RD; width[1:0] = \bit 

  // Notes on the sheet:
  //   00 word
  //   01 half-word
  //   10 byte
endmodule

module SPL (
  input  [31:0] Option,
  output [5:0] func,
  output [4:0] shamt,
  output [4:0] rd,
  output [4:0] rt,
  output [4:0] rs,
  output [5:0] optCode,
  output [15:0] imm16
);


  assign func = Option[5:0];
  assign imm16 = Option[15:0];
  assign optCode = Option[31:26];
  assign rd = Option[15:11];
  assign rs = Option[25:21];
  assign rt = Option[20:16];
  assign shamt = Option[10:6];
endmodule

module Controller (
  input  [5:0] optCode,
  input  [5:0] \function ,
  output out_3,
  output out_4,
  output [1:0] out_5,
  output out_6,
  output out_7,
  output out_8,
  output [1:0] out_9,
  output [2:0] out_10,
  output [1:0] out_11,
  output out_12
);

  wire add, beq, lui, lw, not_1_out, not_3_out, not_4_out, not_5_out, not_9_out, not_10_out, not_13_out,
       not_15_out, not_16_out, not_17_out, not_21_out, not_22_out, ori, sll, special, sub, sw;

  not not_1 (not_1_out, optCode[0]);
  // NOT_Gate not_2 has open pins: in=not_1_out, out=open
  not not_3 (not_3_out, optCode[1]);
  not not_4 (not_4_out, optCode[2]);
  not not_5 (not_5_out, optCode[3]);
  // NOT_Gate not_6 has open pins: in=not_3_out, out=open
  // NOT_Gate not_7 has open pins: in=not_4_out, out=open
  // NOT_Gate not_8 has open pins: in=not_5_out, out=open
  not not_9 (not_9_out, optCode[4]);
  not not_10 (not_10_out, optCode[5]);
  // NOT_Gate not_11 has open pins: in=not_9_out, out=open
  // NOT_Gate not_12 has open pins: in=not_10_out, out=open
  and and_1 (special, not_1_out, not_3_out, not_4_out, not_5_out, not_9_out, not_10_out);
  and and_2 (ori, not_10_out, not_9_out, optCode[3], optCode[2], not_3_out, optCode[0]);
  and and_3 (lw, optCode[5], not_9_out, not_5_out, not_4_out, optCode[1], optCode[0]);
  and and_4 (lui, not_10_out, not_9_out, optCode[3], optCode[2], optCode[1], optCode[0]);
  Comparator #(.width(6), .mode("unsigned")) comparator_1 (.a(6'b101011), .b(optCode), .eq(sw));  // open: gt, lt
  Comparator #(.width(6), .mode("unsigned")) comparator_2 (.a(6'b000100), .b(optCode), .eq(beq));  // open: gt, lt
  not not_13 (not_13_out, \function [0]);
  // NOT_Gate not_14 has open pins: in=not_13_out, out=open
  not not_15 (not_15_out, \function [1]);
  not not_16 (not_16_out, \function [3]);
  not not_17 (not_17_out, \function [2]);
  // NOT_Gate not_18 has open pins: in=not_16_out, out=open
  // NOT_Gate not_19 has open pins: in=not_15_out, out=open
  // NOT_Gate not_20 has open pins: in=not_17_out, out=open
  not not_21 (not_21_out, \function [5]);
  not not_22 (not_22_out, \function [4]);
  // NOT_Gate not_23 has open pins: in=not_21_out, out=open
  // NOT_Gate not_24 has open pins: in=not_22_out, out=open
  and and_5 (add, \function [5], not_22_out, not_16_out, not_17_out, not_15_out, not_13_out, special);
  and and_6 (sub, \function [5], not_22_out, not_16_out, not_17_out, \function [1], not_13_out, special);
  and and_7 (sll, not_13_out, not_15_out, not_17_out, not_16_out, not_22_out, not_21_out, special);
  or or_1 (out_3, add, sub, sll);
  or or_2 (out_4, ori, lw, sw, lui);
  buf MemtoReg (out_5[0], lw);  // OR_Gate
  buf immtoReg (out_5[1], lui);  // OR_Gate
  or or_3 (out_6, add, sub, ori, lw, sll, lui);
  buf or_4 (out_7, sw);  // OR_Gate
  buf or_5 (out_8, beq);  // OR_Gate
  or or_6 (out_9[0], lw, sw, beq);
  buf or_7 (out_9[1], lui);  // OR_Gate
  or or_8 (out_10[0], sub, ori);
  buf or_9 (out_10[1], ori);  // OR_Gate
  buf or_10 (out_10[2], sll);  // OR_Gate
  buf or_11 (out_11[0], 1'b0);  // OR_Gate
  buf or_12 (out_11[1], 1'b0);  // OR_Gate
  buf or_13 (out_12, 1'b0);  // OR_Gate

  // Other names for the same wires on the sheet: ALUSrc = out_4; B_PC_not = out_12; F[5:0] = \function ;
  //   F0 = \function [0]; F1 = \function [1]; F2 = \function [2]; F3 = \function [3]; F4 = \function [4];
  //   F5 = \function [5]; MemWrite = out_7; nPC_sel = out_8; O[5:0] = optCode; O0 = optCode[0]; O1 = optCode[1];
  //   O2 = optCode[2]; O3 = optCode[3]; O4 = optCode[4]; O5 = optCode[5]; MemtoReg = out_5[0]; immtoReg = out_5[1];
  //   ExtOp = out_9[0]; ExtOp_1 = out_9[1]; ALUctr_0 = out_10[0]; ALUctr_1 = out_10[1]; ALUctr_2 = out_10[2];
  //   RAMWidth_0 = out_11[0]; RAMWidth_1 = out_11[1]; RegDst = out_3; RegWrite = out_6

  // Notes on the sheet:
  //   0 reg
  //   1 imm
  //   00 ALUtoReg
  //   01 MemtoReg
  //   10 immtoReg
  //   11 PC+4toReg
  //   ?
  //   00 unsigned
  //   10 tohi
  //   01 signed
endmodule
