// Logisim project 4bit_sort.circ as structural Verilog: 4 circuits, main circuit 1bit_swap
module _1bit_swap (
  input  I1,
  input  I2,
  input  s,
  output O1,
  output O2
);

  wire and_1_out, and_2_out, and_3_out, and_4_out, nots;

  not not_1 (nots, s);
  and and_1 (and_1_out, nots, I1);
  and and_2 (and_2_out, I1, s);
  and and_3 (and_3_out, s, I2);
  and and_4 (and_4_out, I2, nots);
  or or_1 (O1, and_1_out, and_3_out);
  or or_2 (O2, and_2_out, and_4_out);

  // Other names for the same wires on the sheet: iss = s
endmodule

// stag
module _4bit_swap (
  input  [3:0] i1,
  input  [3:0] i2,
  input  s,
  output [3:0] out_4,
  output [3:0] out_5
);

  _1bit_swap u_1bit_swap_1 (.I1(i1[0]), .I2(i2[0]), .s(s), .O1(out_4[0]), .O2(out_5[0]));
  _1bit_swap u_1bit_swap_2 (.I1(i1[1]), .I2(i2[1]), .s(s), .O1(out_4[1]), .O2(out_5[1]));
  _1bit_swap u_1bit_swap_3 (.I1(i1[2]), .I2(i2[2]), .s(s), .O1(out_4[2]), .O2(out_5[2]));
  _1bit_swap u_1bit_swap_4 (.I1(i1[3]), .I2(i2[3]), .s(s), .O1(out_4[3]), .O2(out_5[3]));
endmodule

module _2num_sort (
  input  [3:0] in_1,
  input  [3:0] in_2,
  output [3:0] out_3,
  output [3:0] out_4
);

  wire comparator_1_gt;

  Comparator #(.width(4), .mode("unsigned")) comparator_1 (.a(in_1), .b(in_2), .gt(comparator_1_gt));  // open: eq, lt
  _4bit_swap u_4bit_swap_1 (.i1(in_1), .i2(in_2), .s(comparator_1_gt), .out_4(out_3), .out_5(out_4));
endmodule

module _4bit_sort (
  input  [3:0] in_1,
  input  [3:0] in_2,
  input  [3:0] in_3,
  input  [3:0] in_4,
  output [3:0] out_5,
  output [3:0] out_6,
  output [3:0] out_7,
  output [3:0] out_8
);

  wire [3:0] n2num_sort_1_out_3, n2num_sort_1_out_4, n2num_sort_2_out_3, n2num_sort_2_out_4,
       n2num_sort_3_out_4, n2num_sort_4_out_3, n2num_sort_4_out_4, n2num_sort_5_out_4;

  _2num_sort u_2num_sort_1 (.in_1(in_3), .in_2(in_4), .out_3(n2num_sort_1_out_3), .out_4(n2num_sort_1_out_4));
  _2num_sort u_2num_sort_2 (
    .in_1(in_2), .in_2(n2num_sort_1_out_3), .out_3(n2num_sort_2_out_3), .out_4(n2num_sort_2_out_4));
  _2num_sort u_2num_sort_3 (.in_1(in_1), .in_2(n2num_sort_2_out_3), .out_3(out_5), .out_4(n2num_sort_3_out_4));
  _2num_sort u_2num_sort_4 (
    .in_1(n2num_sort_2_out_4), .in_2(n2num_sort_1_out_4), .out_3(n2num_sort_4_out_3),
    .out_4(n2num_sort_4_out_4));
  _2num_sort u_2num_sort_5 (
    .in_1(n2num_sort_3_out_4), .in_2(n2num_sort_4_out_3), .out_3(out_6), .out_4(n2num_sort_5_out_4));
  _2num_sort u_2num_sort_6 (.in_1(n2num_sort_5_out_4), .in_2(n2num_sort_4_out_4), .out_3(out_7), .out_4(out_8));
endmodule
