// Logisim project fibnacci_2.circ as structural Verilog: 3 circuits, main circuit main
module main (
  input  [2:0] in_1,
  output [3:0] out_2
);

  wire clock_1_out, loop_module_1_out_2, not_1_out, or_1_out, register_1_q;
  wire [3:0] calculate_module_1_out_2;

  Clock clock_1 (.out(clock_1_out));
  Loop_Module loop_module_1 (.in_1(in_1), .out_2(loop_module_1_out_2));
  // Probe on calculate_module_1_out_2
  Calculate_Module calculate_module_1 (.in_1(or_1_out), .out_2(calculate_module_1_out_2));
  not not_1 (not_1_out, register_1_q);
  or or_1 (or_1_out, loop_module_1_out_2, register_1_q);
  Register #(.width(1)) register_1 (
    .D(loop_module_1_out_2), .en(not_1_out), .Q(register_1_q), .clk(clock_1_out));  // open: clr
  Multiplexer #(.width(4)) multiplexer_1 (
    .in0(4'b0000), .in1(calculate_module_1_out_2), .out(out_2), .sel(or_1_out));  // open: en
endmodule

module Calculate_Module (
  input  in_1,
  output [3:0] out_2
);

  wire clk, enable, ini;
  wire [3:0] adder_1_out, multiplexer_1_out, prev;

  not not_1 (enable, in_1);
  Clock clock_1 (.out(clk));
  Multiplexer #(.width(4)) multiplexer_1 (.in0(4'b0001), .in1(out_2), .out(multiplexer_1_out), .sel(ini));  // open: en
  Adder #(.width(4)) adder_1 (.a(out_2), .b(prev), .out(adder_1_out));  // open: cin, cout
  Register #(.width(4)) register_1 (.D(multiplexer_1_out), .en(enable), .Q(prev), .clk(clk), .clr(1'b0));
  Register #(.width(4)) register_2 (.D(adder_1_out), .en(enable), .Q(out_2), .clk(clk), .clr(1'b0));
  Counter #(.width(1), .max('h1), .ongoal("stay")) counter_1 (
    .Q(ini), .clk(clk), .clr(1'b0));  // open: load, D, count, carry

  // Other names for the same wires on the sheet: now[3:0] = out_2
endmodule

module Loop_Module (
  input  [2:0] in_1,
  output out_2
);

  wire clk;
  wire [3:0] bit_extender_1_out, counter_1_q;

  Clock clock_1 (.out(clk));
  Counter #(.width(4), .max('hf)) counter_1 (.Q(counter_1_q), .clk(clk));  // open: load, D, count, carry, clr
  assign bit_extender_1_out = {{1{1'b0}}, in_1};  // Bit_Extender bit_extender_1
  Comparator #(.width(4), .mode("unsigned")) comparator_1 (
    .a(bit_extender_1_out), .b(counter_1_q), .lt(out_2));  // open: gt, eq
endmodule
