// Logisim project fibnacci_32bit.circ as structural Verilog: 5 circuits, main circuit main
module main (
  input  [31:0] in_1,
  output [31:0] out_2
);

  wire clk, enable, isBegin, not_1_out, reset, sig, stop;
  wire [31:0] matmult_1_out_9, matmult_1_out_10, matmult_1_out_11, matmult_1_out_12, matmult_2_out_9,
       matmult_2_out_10, matmult_2_out_11, matmult_2_out_12, matreg_1_out_6, matreg_1_out_7, matreg_1_out_8,
       matreg_1_out_9, matreg_2_out_6, matreg_2_out_7, matreg_2_out_8, matreg_2_out_9, matX_1_1, matX_1_2,
       matX_2_1, matX_2_2, quadmux_2_out_10, quadmux_2_out_11, quadmux_2_out_12, quadmux_2_out_13,
       quadmux_3_out_10, quadmux_3_out_11, quadmux_3_out_12, quadmux_3_out_13;

  Clock clock_1 (.out(clk));
  not not_1 (not_1_out, reset);
  Counter #(.width(1), .max('h1), .ongoal("stay")) counter_1 (
    .Q(isBegin), .clk(clk));  // open: load, D, count, carry, clr
  Register #(.width(1)) register_1 (.D(stop), .en(not_1_out), .Q(reset), .clk(clk));  // open: clr
  poiter poiter_1 (.in_1(in_1), .in_2(reset), .out_3(sig), .out_4(stop));
  not not_2 (enable, reset);
  matReg matreg_1 (
    .in_1(matmult_1_out_9), .in_2(matmult_1_out_10), .in_3(matmult_1_out_11), .in_4(matmult_1_out_12),
    .in_5(enable), .out_6(matreg_1_out_6), .out_7(matreg_1_out_7), .out_8(matreg_1_out_8),
    .out_9(matreg_1_out_9));
  matReg matreg_2 (
    .in_1(matmult_2_out_9), .in_2(matmult_2_out_10), .in_3(matmult_2_out_11), .in_4(matmult_2_out_12),
    .in_5(enable), .out_6(matreg_2_out_6), .out_7(matreg_2_out_7), .out_8(matreg_2_out_8),
    .out_9(matreg_2_out_9));
  // Probe on matmult_2_out_10
  quadMux quadmux_1 (
    .in_1(32'h1), .in_2(32'h1), .in_3(32'h1), .in_4({32{1'b0}}), .in_5(matreg_1_out_6),
    .in_6(matreg_1_out_7), .in_7(matreg_1_out_8), .in_8(matreg_1_out_9), .in_9(isBegin), .out_10(matX_1_1),
    .out_11(matX_1_2), .out_12(matX_2_1), .out_13(matX_2_2));
  quadMux quadmux_2 (
    .in_1(32'h1), .in_2({32{1'b0}}), .in_3({32{1'b0}}), .in_4({32{1'b0}}), .in_5(matreg_2_out_6),
    .in_6(matreg_2_out_7), .in_7(matreg_2_out_8), .in_8(matreg_2_out_9), .in_9(isBegin),
    .out_10(quadmux_2_out_10), .out_11(quadmux_2_out_11), .out_12(quadmux_2_out_12), .out_13(quadmux_2_out_13));
  // Probe on matX_1_1
  // Probe on matmult_2_out_9
  // Probe on matmult_2_out_11
  // Probe on matmult_2_out_12
  // Probe on matX_2_2
  // Probe on matX_2_1
  // Probe on matX_1_2
  matMult matmult_1 (
    .in_1(matX_1_1), .in_2(matX_1_2), .in_3(matX_2_1), .in_4(matX_2_2), .in_5(matX_1_1), .in_6(matX_1_2),
    .in_7(matX_2_1), .in_8(matX_2_2), .out_9(matmult_1_out_9), .out_10(matmult_1_out_10),
    .out_11(matmult_1_out_11), .out_12(matmult_1_out_12));
  quadMux quadmux_3 (
    .in_1(32'h1), .in_2({32{1'b0}}), .in_3({32{1'b0}}), .in_4(32'h1), .in_5(matX_1_1), .in_6(matX_1_2),
    .in_7(matX_2_1), .in_8(matX_2_2), .in_9(sig), .out_10(quadmux_3_out_10), .out_11(quadmux_3_out_11),
    .out_12(quadmux_3_out_12), .out_13(quadmux_3_out_13));
  Multiplexer #(.width(32)) multiplexer_1 (
    .in0({32{1'b0}}), .in1(matmult_2_out_10), .out(out_2), .sel(reset));  // open: en
  matMult matmult_2 (
    .in_1(quadmux_2_out_10), .in_2(quadmux_2_out_11), .in_3(quadmux_2_out_12), .in_4(quadmux_2_out_13),
    .in_5(quadmux_3_out_10), .in_6(quadmux_3_out_11), .in_7(quadmux_3_out_12), .in_8(quadmux_3_out_13),
    .out_9(matmult_2_out_9), .out_10(matmult_2_out_10), .out_11(matmult_2_out_11), .out_12(matmult_2_out_12));
endmodule

module matMult (
  input  [31:0] in_1,
  input  [31:0] in_2,
  input  [31:0] in_3,
  input  [31:0] in_4,
  input  [31:0] in_5,
  input  [31:0] in_6,
  input  [31:0] in_7,
  input  [31:0] in_8,
  output [31:0] out_9,
  output [31:0] out_10,
  output [31:0] out_11,
  output [31:0] out_12
);

  wire [31:0] multiplier_1_out, multiplier_2_out, multiplier_3_out, multiplier_4_out, multiplier_5_out,
       multiplier_6_out, multiplier_7_out, multiplier_8_out;

  Multiplier #(.width(32)) multiplier_1 (.a(in_1), .b(in_5), .out(multiplier_1_out));  // open: cin, cout
  Multiplier #(.width(32)) multiplier_2 (.a(in_2), .b(in_7), .out(multiplier_2_out));  // open: cin, cout
  Multiplier #(.width(32)) multiplier_3 (.a(in_6), .b(in_3), .out(multiplier_3_out));  // open: cin, cout
  Multiplier #(.width(32)) multiplier_4 (.a(in_4), .b(in_8), .out(multiplier_4_out));  // open: cin, cout
  Multiplier #(.width(32)) multiplier_5 (.a(in_1), .b(in_6), .out(multiplier_5_out));  // open: cin, cout
  Multiplier #(.width(32)) multiplier_6 (.a(in_2), .b(in_8), .out(multiplier_6_out));  // open: cin, cout
  Multiplier #(.width(32)) multiplier_7 (.a(in_5), .b(in_3), .out(multiplier_7_out));  // open: cin, cout
  Multiplier #(.width(32)) multiplier_8 (.a(in_7), .b(in_4), .out(multiplier_8_out));  // open: cin, cout
  Adder #(.width(32)) adder_1 (.a(multiplier_1_out), .b(multiplier_2_out), .out(out_9));  // open: cin, cout
  Adder #(.width(32)) adder_2 (.a(multiplier_3_out), .b(multiplier_4_out), .out(out_12));  // open: cin, cout
  Adder #(.width(32)) adder_3 (.a(multiplier_5_out), .b(multiplier_6_out), .out(out_10));  // open: cin, cout
  Adder #(.width(32)) adder_4 (.a(multiplier_7_out), .b(multiplier_8_out), .out(out_11));  // open: cin, cout

  // Other names for the same wires on the sheet: matA_1_1[31:0] = in_1; matA_1_2[31:0] = in_2; matA_2_1[31:0] = in_3;
  //   matA_2_2[31:0] = in_4; matB_1_1[31:0] = in_5; matB_1_2[31:0] = in_6; matB_2_1[31:0] = in_7;
  //   matB_2_2[31:0] = in_8; matC_1_1[31:0] = out_9; matC_1_2[31:0] = out_10; matC_2_1[31:0] = out_11;
  //   matC_2_2[31:0] = out_12
endmodule

module poiter (
  input  [31:0] in_1,
  input  in_2,
  output out_3,
  output out_4
);

  wire bitselector_1_out, clk, not_1_out;
  wire [4:0] counter_1_q;

  Clock clock_1 (.out(clk));
  Counter #(.width(5), .max('h1f), .ongoal("stay")) counter_1 (
    .Q(counter_1_q), .clk(clk));  // open: load, D, count, carry, clr
  BitSelector #(.width(32)) bitselector_1 (.in(in_1), .out(bitselector_1_out), .sel(counter_1_q));
  not not_1 (not_1_out, in_2);
  // NOT_Gate not_2 is placed but not wired
  Comparator #(.width(5)) comparator_1 (.a(counter_1_q), .b({5{1'b1}}), .eq(out_4));  // open: gt, lt
  and and_1 (out_3, bitselector_1_out, not_1_out);

  // Other names for the same wires on the sheet: reset = in_2
endmodule

module matReg (
  input  [31:0] in_1,
  input  [31:0] in_2,
  input  [31:0] in_3,
  input  [31:0] in_4,
  input  in_5,
  output [31:0] out_6,
  output [31:0] out_7,
  output [31:0] out_8,
  output [31:0] out_9
);

  wire clk;

  Clock clock_1 (.out(clk));
  Register #(.width(32)) register_1 (.D(in_1), .en(in_5), .Q(out_6), .clk(clk));  // open: clr
  Register #(.width(32)) register_2 (.D(in_2), .en(in_5), .Q(out_7), .clk(clk));  // open: clr
  Register #(.width(32)) register_3 (.D(in_3), .en(in_5), .Q(out_8), .clk(clk));  // open: clr
  Register #(.width(32)) register_4 (.D(in_4), .en(in_5), .Q(out_9), .clk(clk));  // open: clr

  // Other names for the same wires on the sheet: enable = in_5
endmodule

module quadMux (
  input  [31:0] in_1,
  input  [31:0] in_2,
  input  [31:0] in_3,
  input  [31:0] in_4,
  input  [31:0] in_5,
  input  [31:0] in_6,
  input  [31:0] in_7,
  input  [31:0] in_8,
  input  in_9,
  output [31:0] out_10,
  output [31:0] out_11,
  output [31:0] out_12,
  output [31:0] out_13
);

  Multiplexer #(.width(32)) multiplexer_1 (.in0(in_1), .in1(in_5), .out(out_10), .sel(in_9));  // open: en
  Multiplexer #(.width(32)) multiplexer_2 (.in0(in_2), .in1(in_6), .out(out_11), .sel(in_9));  // open: en
  Multiplexer #(.width(32)) multiplexer_3 (.in0(in_3), .in1(in_7), .out(out_12), .sel(in_9));  // open: en
  Multiplexer #(.width(32)) multiplexer_4 (.in0(in_4), .in1(in_8), .out(out_13), .sel(in_9));  // open: en

  // Other names for the same wires on the sheet: sele = in_9
endmodule
