// Logisim project mod5.circ as structural Verilog: 4 circuits, main circuit mod5
module mod5 (
  input  in_1,
  output out_2,
  output out_3,
  output out_4,
  output out_5,
  output out_6
);

  wire clock_1_out;
  wire [1:0] logicnetwork_1_out_3, statereg_1_out_3;

  Clock clock_1 (.out(clock_1_out));
  LogicNetwork logicnetwork_1 (.in_1(in_1), .in_2(statereg_1_out_3), .out_3(logicnetwork_1_out_3));
  // Probe on statereg_1_out_3
  StateReg statereg_1 (.in_1(logicnetwork_1_out_3), .in_2(clock_1_out), .out_3(statereg_1_out_3));
  OnehotPlexer onehotplexer_1 (
    .in_1(statereg_1_out_3), .in_2(in_1), .out_3(out_2), .out_4(out_3), .out_5(out_4), .out_6(out_5),
    .out_7(out_6));
endmodule

module LogicNetwork (
  input  in_1,
  input  [1:0] in_2,
  output [1:0] out_3
);


  assign out_3 = {in_2[0], in_1};
endmodule

module StateReg (
  input  [1:0] in_1,
  input  in_2,
  output [1:0] out_3
);

  Register #(.width(2)) register_1 (.D(in_1), .Q(out_3), .clk(in_2));  // open: en, clr
endmodule

module OnehotPlexer (
  input  [1:0] in_1,
  input  in_2,
  output out_3,
  output out_4,
  output out_5,
  output out_6,
  output out_7
);

  wire [1:0] logicnetwork_1_out_3;

  LogicNetwork logicnetwork_1 (.in_1(in_2), .in_2(in_1), .out_3(logicnetwork_1_out_3));
  Decoder #(.select(2)) decoder_1 (
    .out0(out_4), .out1(out_5), .out2(out_7), .out3(out_6), .sel(logicnetwork_1_out_3));  // open: en

  assign out_3 = 1'b0;
endmodule
