// Logisim project swap.circ as structural Verilog: 1 circuit, main circuit swap
module swap (
  input  I1,
  input  I2,
  input  s,
  output O1,
  output O2
);

  wire and_1_out, and_2_out, and_3_out, and_4_out, nots;

  not not_1 (nots, s);
  and and_1 (and_1_out, nots, I1);
  and and_2 (and_2_out, I1, s);
  and and_3 (and_3_out, s, I2);
  and and_4 (and_4_out, I2, nots);
  or or_1 (O1, and_1_out, and_3_out);
  or or_2 (O2, and_2_out, and_4_out);

  // Other names for the same wires on the sheet: iss = s
endmodule
